// Logisim project CPU.circ as structural Verilog: 16 circuits, main circuit CPU
module REG4 (
  input  PR,
  input  CLR,
  input  CLK,
  input  D1,
  input  D2,
  input  D3,
  input  D4,
  output Q1,
  output Q2,
  output Q3,
  output Q4,
  output Q1_NOT,
  output Q2_NOT,
  output Q3_NOT,
  output Q4_NOT
);

  D_Flip_Flop d_ff_1 (.clk(CLK), .D(D1), .Q(Q1), .Qn(Q1_NOT), .preset(PR), .reset(CLR));
  D_Flip_Flop d_ff_2 (.clk(CLK), .D(D2), .Q(Q2), .Qn(Q2_NOT), .preset(PR), .reset(CLR));
  D_Flip_Flop d_ff_3 (.clk(CLK), .D(D3), .Q(Q3), .Qn(Q3_NOT), .preset(PR), .reset(CLR));
  D_Flip_Flop d_ff_4 (.clk(CLK), .D(D4), .Q(Q4), .Qn(Q4_NOT), .preset(PR), .reset(CLR));

  // Notes on the sheet:
  //   Registrador Paralelo
endmodule

module CPU (
);

  wire K0, K1, K2, K3, L0, L1, L2, L3, L4, L5, L6, L7, L8, L9, or_1_out, or_2_out, RESET_PC, RESET_REG, S0,
       S1, S2, S3, S4, S5, S6, S7, S8, S9;
  wire [1:0] CU_rgin, CU_rgto, HEX3;
  wire [3:0] HEX0, HEX1, HEX2, HEX4, HEX5, multiplexer_1_out, TO_REG1, TO_REG2, ULA_r;
  wire [7:0] counter8_jmp_1_q;
  wire [15:0] REG16_q, ROM_data;

  LED u_L9 (.in(L9));
  // DipSwitch #(.NSwitches(1)) S9: pin names not known; wires that end beside it: S9
  or or_1 (or_1_out, S0, RESET_PC);
  Hex_Digit_Display hex_digit_display_1 (.value(HEX5));  // open: dp
  Hex_Digit_Display hex_digit_display_2 (.value(HEX4));  // open: dp
  LED u_L7 (.in(L7));
  LED u_L8 (.in(L8));
  // DipSwitch #(.NSwitches(1)) S6: pin names not known; wires that end beside it: S6
  // DipSwitch #(.NSwitches(1)) S7: pin names not known; wires that end beside it: S7
  // DipSwitch #(.NSwitches(1)) S8: pin names not known; wires that end beside it: S8
  COUNTER8_JMP counter8_jmp_1 (.CLK(S9), .Vcc(1'b1), .JMP(L0), .X(HEX1), .CLR(or_1_out), .Q(counter8_jmp_1_q));
  Hex_Digit_Display hex_digit_display_3 (.value(HEX2));  // open: dp
  Hex_Digit_Display hex_digit_display_4 (.value({2'b00, HEX3}));  // open: dp
  LED u_L6 (.in(L6));
  LED u_L5 (.in(L5));
  LED u_L4 (.in(L4));
  // DipSwitch #(.NSwitches(1)) S5: pin names not known; wires that end beside it: S5
  // DipSwitch #(.NSwitches(1)) S4: pin names not known; wires that end beside it: S4
  Hex_Digit_Display hex_digit_display_5 (.value(HEX1));  // open: dp
  LED u_L3 (.in(L3));
  LED u_L1 (.in(L1));
  LED u_L2 (.in(L2));
  // DipSwitch #(.NSwitches(1)) S1: pin names not known; wires that end beside it: S1
  // DipSwitch #(.NSwitches(1)) S2: pin names not known; wires that end beside it: S2
  // DipSwitch #(.NSwitches(1)) S3: pin names not known; wires that end beside it: S3
  REG16 REG16 (.D(ROM_data), .Clock(S9), .Q(REG16_q));  // open: Preset, Clear
  ROM #(.dataWidth(16), .Select("low")) ROM (.addr(counter8_jmp_1_q), .data(ROM_data));
  REG4_Grouped REG1 (.CLK(S9), .D(TO_REG1), .Clear(or_2_out), .Q(HEX2));  // open: Preset, Q_NOT
  Hex_Digit_Display hex_digit_display_6 (.value(HEX0));  // open: dp
  LED u_L0 (.in(L0));
  // DipSwitch #(.NSwitches(1)) S0: pin names not known; wires that end beside it: S0
  Button u_K3 (.out(K3));
  Multiplexer #(.select(2), .width(4), .enable("false")) multiplexer_1 (
    .in0(4'b0000), .in1(HEX2), .in2(HEX0), .in3(4'b0000), .out(multiplexer_1_out), .sel(CU_rgin));
  CONTROL_UNIT CU (
    .dataBus_16(REG16_q), .RgIN(CU_rgin), .X(HEX1), .ULA(HEX3), .RgTO(CU_rgto), .JMP_RESET_REG(RESET_REG),
    .JMP_RESET_PC(RESET_PC), .JMP_X(L0));  // open: NULL, JMP_ULA
  or or_2 (or_2_out, S0, RESET_PC);
  Button u_K0 (.out(K0));
  Button u_K2 (.out(K2));
  Button u_K1 (.out(K1));
  ULA ULA (.A(multiplexer_1_out), .B(HEX1), .Op(HEX3), .R(ULA_r));
  REG4_Grouped REG2 (.CLK(S9), .D(TO_REG2), .Clear(or_2_out), .Q(HEX0));  // open: Preset, Q_NOT
  Demultiplexer #(.select(2), .width(4), .enable("false")) demultiplexer_1 (
    .out1(TO_REG1), .out2(TO_REG2), .in(ULA_r), .sel(CU_rgto));  // open: out0, out3

  // Other names for the same wires on the sheet: MEM_JMP = L0; Q_REG1[3:0] = HEX2; Q_REG2[3:0] = HEX0; X[3:0] = HEX1

  // Notes on the sheet:
  //   CLK
  //   Counter com JUMP
  //   S0 = CLR, S9 = CLK
  //   ULA
  //   REG1
  //   X
  //   contents of ROM (hex, n*v repeats v):
  //   4103 9202 6001 4307 15*0 800
  //   REG2
  //   MEM_JMP
  //   CLR
  //   Escolhe o Reg que vai para ULA
  //   A = Q_RgIN
  //   B = X
  //   Escolhe o Reg no qual será guardado o resultado
endmodule

module COUNTER8 (
  input  CLR,
  input  CLK,
  input  Vcc,
  output [7:0] Q
);

  wire and_6_out, T2, T3, T4, T5, T6;

  T_Flip_Flop t_ff_1 (.clk(CLK), .T(Vcc), .Q(Q[0]), .reset(CLR));  // open: Qn, preset
  T_Flip_Flop t_ff_2 (.clk(CLK), .T(Q[0]), .Q(Q[1]), .reset(CLR));  // open: Qn, preset
  and and_1 (T2, Q[0], Q[1]);
  T_Flip_Flop t_ff_3 (.clk(CLK), .T(T2), .Q(Q[2]), .reset(CLR));  // open: Qn, preset
  and and_2 (T3, T2, Q[2]);
  T_Flip_Flop t_ff_4 (.clk(CLK), .T(T3), .Q(Q[3]), .reset(CLR));  // open: Qn, preset
  and and_3 (T4, T3, Q[3]);
  T_Flip_Flop t_ff_5 (.clk(CLK), .T(T4), .Q(Q[4]), .reset(CLR));  // open: Qn, preset
  and and_4 (T5, T4, Q[4]);
  T_Flip_Flop t_ff_6 (.clk(CLK), .T(T5), .Q(Q[5]), .reset(CLR));  // open: Qn, preset
  and and_5 (T6, T5, Q[5]);
  T_Flip_Flop t_ff_7 (.clk(CLK), .T(T6), .Q(Q[6]), .reset(CLR));  // open: Qn, preset
  and and_6 (and_6_out, T6, Q[6]);
  T_Flip_Flop t_ff_8 (.clk(CLK), .T(and_6_out), .Q(Q[7]), .reset(CLR));  // open: Qn, preset

  // Notes on the sheet:
  //   Contador de 8 Bits Síncrono
endmodule

module ROM16x16 (
  input  Clock,
  output [3:0] Address,
  output [15:0] Word
);

  wire and_1_out, and_2_out, and_3_out, and_4_out, and_5_out, and_6_out, and_7_out, and_8_out, and_9_out,
       and_10_out, and_11_out, and_12_out, and_13_out, and_14_out, and_15_out, and_16_out,
       demultiplexer_1_out0, demultiplexer_1_out1, demultiplexer_1_out2, demultiplexer_1_out3,
       demultiplexer_2_out0, demultiplexer_2_out1, demultiplexer_2_out2, demultiplexer_2_out3;
  wire [3:0] undriven, undriven_2;
  wire [15:0] reg16_1_q, reg16_2_q, reg16_3_q, reg16_4_q, reg16_5_q, reg16_6_q, reg16_7_q, reg16_8_q,
       reg16_9_q, reg16_10_q, reg16_11_q, reg16_12_q, reg16_13_q, reg16_14_q, reg16_15_q, reg16_16_q;

  // DipSwitch A3_A2_A1_A0: pin names not known; wires that end beside it: Address[3], Address[2], Address[1], 1'b1, Address[0]
  Demultiplexer #(.select(2), .enable("false")) demultiplexer_1 (
    .out0(demultiplexer_1_out0), .out1(demultiplexer_1_out1), .out2(demultiplexer_1_out2),
    .out3(demultiplexer_1_out3), .in(1'b1), .sel(Address[1:0]));
  Demultiplexer #(.select(2), .enable("false")) demultiplexer_2 (
    .out0(demultiplexer_2_out0), .out1(demultiplexer_2_out1), .out2(demultiplexer_2_out2),
    .out3(demultiplexer_2_out3), .in(1'b1), .sel(Address[3:2]));
  Hex_Digit_Display hex_digit_display_1 (.value(undriven));  // open: dp
  Hex_Digit_Display hex_digit_display_2 (.value(undriven_2));  // open: dp
  LED led_1 (.in(and_1_out));
  and and_1 (and_1_out, demultiplexer_1_out0, demultiplexer_2_out0);
  REG16 reg16_1 (.D({16{1'b0}}), .Clock(Clock), .Q(reg16_1_q));  // open: Preset, Clear
  LED led_2 (.in(and_2_out));
  and and_2 (and_2_out, demultiplexer_1_out1, demultiplexer_2_out0);
  LED led_3 (.in(and_3_out));
  and and_3 (and_3_out, demultiplexer_1_out2, demultiplexer_2_out0);
  and and_4 (and_4_out, demultiplexer_1_out3, demultiplexer_2_out0);
  assign Word = and_1_out ? reg16_1_q : 16'bz;  // Controlled_Buffer controlled_buffer_1
  assign Word = and_2_out ? reg16_2_q : 16'bz;  // Controlled_Buffer controlled_buffer_2
  REG16 reg16_2 (.D(16'h1), .Clock(Clock), .Q(reg16_2_q));  // open: Preset, Clear
  assign Word = and_3_out ? reg16_3_q : 16'bz;  // Controlled_Buffer controlled_buffer_3
  REG16 reg16_3 (.D(16'h2), .Clock(Clock), .Q(reg16_3_q));  // open: Preset, Clear
  assign Word = and_4_out ? reg16_4_q : 16'bz;  // Controlled_Buffer controlled_buffer_4
  LED led_4 (.in(and_4_out));
  REG16 reg16_4 (.D(16'h3), .Clock(Clock), .Q(reg16_4_q));  // open: Preset, Clear
  LED led_5 (.in(and_5_out));
  and and_5 (and_5_out, demultiplexer_1_out0, demultiplexer_2_out1);
  and and_6 (and_6_out, demultiplexer_1_out1, demultiplexer_2_out1);
  assign Word = and_5_out ? reg16_5_q : 16'bz;  // Controlled_Buffer controlled_buffer_5
  REG16 reg16_5 (.D(16'h4), .Clock(Clock), .Q(reg16_5_q));  // open: Preset, Clear
  assign Word = and_6_out ? reg16_6_q : 16'bz;  // Controlled_Buffer controlled_buffer_6
  LED led_6 (.in(and_6_out));
  REG16 reg16_6 (.D(16'h5), .Clock(Clock), .Q(reg16_6_q));  // open: Preset, Clear
  LED led_7 (.in(and_7_out));
  and and_7 (and_7_out, demultiplexer_1_out2, demultiplexer_2_out1);
  REG16 reg16_7 (.D(16'h6), .Clock(Clock), .Q(reg16_7_q));  // open: Preset, Clear
  LED led_8 (.in(and_8_out));
  and and_8 (and_8_out, demultiplexer_1_out3, demultiplexer_2_out1);
  assign Word = and_7_out ? reg16_7_q : 16'bz;  // Controlled_Buffer controlled_buffer_7
  assign Word = and_8_out ? reg16_8_q : 16'bz;  // Controlled_Buffer controlled_buffer_8
  REG16 reg16_8 (.D(16'h7), .Clock(Clock), .Q(reg16_8_q));  // open: Preset, Clear
  LED led_9 (.in(and_9_out));
  and and_9 (and_9_out, demultiplexer_1_out0, demultiplexer_2_out2);
  REG16 reg16_9 (.D(16'h8), .Clock(Clock), .Q(reg16_9_q));  // open: Preset, Clear
  LED led_10 (.in(and_10_out));
  and and_10 (and_10_out, demultiplexer_1_out1, demultiplexer_2_out2);
  LED led_11 (.in(and_11_out));
  and and_11 (and_11_out, demultiplexer_1_out2, demultiplexer_2_out2);
  and and_12 (and_12_out, demultiplexer_1_out3, demultiplexer_2_out2);
  assign Word = and_9_out ? reg16_9_q : 16'bz;  // Controlled_Buffer controlled_buffer_9
  assign Word = and_10_out ? reg16_10_q : 16'bz;  // Controlled_Buffer controlled_buffer_10
  REG16 reg16_10 (.D(16'h9), .Clock(Clock), .Q(reg16_10_q));  // open: Preset, Clear
  assign Word = and_11_out ? reg16_11_q : 16'bz;  // Controlled_Buffer controlled_buffer_11
  REG16 reg16_11 (.D(16'ha), .Clock(Clock), .Q(reg16_11_q));  // open: Preset, Clear
  assign Word = and_12_out ? reg16_12_q : 16'bz;  // Controlled_Buffer controlled_buffer_12
  LED led_12 (.in(and_12_out));
  REG16 reg16_12 (.D(16'hb), .Clock(Clock), .Q(reg16_12_q));  // open: Preset, Clear
  LED led_13 (.in(and_13_out));
  and and_13 (and_13_out, demultiplexer_1_out0, demultiplexer_2_out3);
  and and_14 (and_14_out, demultiplexer_1_out1, demultiplexer_2_out3);
  assign Word = and_13_out ? reg16_13_q : 16'bz;  // Controlled_Buffer controlled_buffer_13
  REG16 reg16_13 (.D(16'hc), .Clock(Clock), .Q(reg16_13_q));  // open: Preset, Clear
  assign Word = and_14_out ? reg16_14_q : 16'bz;  // Controlled_Buffer controlled_buffer_14
  LED led_14 (.in(and_14_out));
  REG16 reg16_14 (.D(16'hd), .Clock(Clock), .Q(reg16_14_q));  // open: Preset, Clear
  LED led_15 (.in(and_15_out));
  and and_15 (and_15_out, demultiplexer_1_out2, demultiplexer_2_out3);
  REG16 reg16_15 (.D(16'he), .Clock(Clock), .Q(reg16_15_q));  // open: Preset, Clear
  LED led_16 (.in(and_16_out));
  and and_16 (and_16_out, demultiplexer_1_out3, demultiplexer_2_out3);
  assign Word = and_15_out ? reg16_15_q : 16'bz;  // Controlled_Buffer controlled_buffer_15
  assign Word = and_16_out ? reg16_16_q : 16'bz;  // Controlled_Buffer controlled_buffer_16
  REG16 reg16_16 (.D(16'hf), .Clock(Clock), .Q(reg16_16_q));  // open: Preset, Clear

  // Notes on the sheet:
  //   ROM 16x16
  //   Lines
  //   Columns
  //   Line 0
  //   Line 1
  //   Line 2
  //   Line 3
  //   Column 0
  //   Column 1
  //   Column 2
  //   Column 3
endmodule

module REG16 (
  input  Preset,
  input  Clock,
  input  [15:0] D,
  input  Clear,
  output [15:0] Q
);

  REG4 reg4_1 (
    .CLK(Clock), .D1(D[0]), .D2(D[1]), .D3(D[2]), .D4(D[3]), .PR(Preset), .CLR(Clear), .Q1(Q[0]), .Q2(Q[1]),
    .Q3(Q[2]), .Q4(Q[3]));  // open: Q1_NOT, Q2_NOT, Q3_NOT, Q4_NOT
  REG4 reg4_2 (
    .CLK(Clock), .D1(D[4]), .D2(D[5]), .D3(D[6]), .D4(D[7]), .PR(Preset), .CLR(Clear), .Q1(Q[4]), .Q2(Q[5]),
    .Q3(Q[6]), .Q4(Q[7]));  // open: Q1_NOT, Q2_NOT, Q3_NOT, Q4_NOT
  REG4 reg4_3 (
    .CLK(Clock), .D1(D[8]), .D2(D[9]), .D3(D[10]), .D4(D[11]), .PR(Preset), .CLR(Clear), .Q1(Q[8]),
    .Q2(Q[9]), .Q3(Q[10]), .Q4(Q[11]));  // open: Q1_NOT, Q2_NOT, Q3_NOT, Q4_NOT
  REG4 reg4_4 (
    .CLK(Clock), .D1(D[12]), .D2(D[13]), .D3(D[14]), .D4(D[15]), .PR(Preset), .CLR(Clear), .Q1(Q[12]),
    .Q2(Q[13]), .Q3(Q[14]), .Q4(Q[15]));  // open: Q1_NOT, Q2_NOT, Q3_NOT, Q4_NOT

  // Other names for the same wires on the sheet: CLK = Clock; CLR = Clear; PR = Preset
endmodule

module REG4_Grouped (
  input  Preset,
  input  CLK,
  input  [3:0] D,
  input  Clear,
  output [3:0] Q,
  output [3:0] Q_NOT
);

  REG4 reg4_1 (
    .CLK(CLK), .D1(D[0]), .D2(D[1]), .D3(D[2]), .D4(D[3]), .PR(Preset), .CLR(Clear), .Q1(Q[0]), .Q2(Q[1]),
    .Q3(Q[2]), .Q4(Q[3]), .Q1_NOT(Q_NOT[0]), .Q2_NOT(Q_NOT[1]), .Q3_NOT(Q_NOT[2]), .Q4_NOT(Q_NOT[3]));
endmodule

module ULA (
  input  [3:0] A,
  input  [3:0] B,
  input  [1:0] Op,
  output [3:0] R
);

  wire [3:0] divider_1_out, multiplier_1_out, or_1_out, subtractor_1_out;

  assign or_1_out = A | B;  // OR_Gate or_1, 4 bits wide
  Multiplier #(.width(4)) multiplier_1 (.a(B), .b(4'b0010), .out(multiplier_1_out));  // open: cin, cout
  Subtractor #(.width(4)) subtractor_1 (.a(A), .b(B), .out(subtractor_1_out));  // open: bin, bout
  Divider #(.width(4)) divider_1 (.a(B), .b(4'b0010), .out(divider_1_out));  // open: upper, rem
  Multiplexer #(.select(2), .width(4), .enable("false")) multiplexer_1 (
    .in0(or_1_out), .in1(multiplier_1_out), .in2(subtractor_1_out), .in3(divider_1_out), .out(R), .sel(Op));

  // Notes on the sheet:
  //   A = REG_IN
  //   B = Operando
  //   REG_in + oper
  //   Opera * 2
  //   REG_in - oper
  //   Operan / 2
endmodule

module CONTROL_UNIT (
  input  [15:0] dataBus_16,
  output [1:0] RgIN,
  output [3:0] X,
  output [3:0] NULL,
  output [1:0] ULA,
  output [1:0] RgTO,
  output JMP_ULA,
  output JMP_RESET_REG,
  output JMP_RESET_PC,
  output JMP_X
);

  Demultiplexer #(.select(2), .enable("false")) demultiplexer_1 (
    .out0(JMP_ULA), .out1(JMP_RESET_REG), .out2(JMP_RESET_PC), .out3(JMP_X), .in(1'b1),
    .sel(dataBus_16[11:10]));

  assign NULL = dataBus_16[7:4];
  assign RgIN = dataBus_16[13:12];
  assign RgTO = dataBus_16[15:14];
  assign ULA = dataBus_16[9:8];
  assign X = dataBus_16[3:0];

  // Notes on the sheet:
  //   -> Memoria vazia
  //   -> Operando, valor generico usado em operações da ULA e de JUMP
endmodule

module COUNTER8_JMP (
  input  JMP,
  input  [3:0] X,
  input  CLR,
  input  CLK,
  input  Vcc,
  output [7:0] Q
);

  wire and_6_out, T2, T3, T4, T5, T6;

  COUNTER8_JMP_UNIT counter8_jmp_unit_1 (.CLK(CLK), .T(Vcc), .X(X[0]), .CLR(CLR), .JMP(JMP), .Q(Q[0]));  // open: Q_NOT
  COUNTER8_JMP_UNIT counter8_jmp_unit_2 (.CLK(CLK), .T(Q[0]), .X(X[1]), .CLR(CLR), .JMP(JMP), .Q(Q[1]));  // open: Q_NOT
  and and_1 (T2, Q[0], Q[1]);
  COUNTER8_JMP_UNIT counter8_jmp_unit_3 (.CLK(CLK), .T(T2), .X(X[2]), .CLR(CLR), .JMP(JMP), .Q(Q[2]));  // open: Q_NOT
  and and_2 (T3, T2, Q[2]);
  COUNTER8_JMP_UNIT counter8_jmp_unit_4 (.CLK(CLK), .T(T3), .X(X[3]), .CLR(CLR), .JMP(JMP), .Q(Q[3]));  // open: Q_NOT
  and and_3 (T4, T3, Q[3]);
  T_Flip_Flop t_ff_1 (.clk(CLK), .T(T4), .Q(Q[4]), .reset(CLR));  // open: Qn, preset
  and and_4 (T5, T4, Q[4]);
  T_Flip_Flop t_ff_2 (.clk(CLK), .T(T5), .Q(Q[5]), .reset(CLR));  // open: Qn, preset
  and and_5 (T6, T5, Q[5]);
  T_Flip_Flop t_ff_3 (.clk(CLK), .T(T6), .Q(Q[6]), .reset(CLR));  // open: Qn, preset
  and and_6 (and_6_out, T6, Q[6]);
  T_Flip_Flop t_ff_4 (.clk(CLK), .T(and_6_out), .Q(Q[7]), .reset(CLR));  // open: Qn, preset

  // Notes on the sheet:
  //   Contador de 8 Bits Síncrono com JUMP
endmodule

module Ativ01 (
);

  wire clock_1_out, d_ff_1_q, K0, K1, K2, K3, L0, L1, L2, L3, L4, L5, L6, L7, L8, L9, S0, S1, S2, S3, S4, S5,
       S6, S7, S8, S9, t_ff_1_q;
  wire [3:0] HEX0, HEX1, HEX2, HEX3, HEX4, HEX5;

  Clock clock_1 (.out(clock_1_out));
  Hex_Digit_Display hex_digit_display_1 (.value(HEX5));  // open: dp
  LED u_L9 (.in(L9));
  LED u_L8 (.in(L8));
  // DipSwitch #(.NSwitches(1)) S7: pin names not known; wires that end beside it: S7
  // DipSwitch #(.NSwitches(1)) S8: pin names not known; wires that end beside it: S8
  // DipSwitch #(.NSwitches(1)) S9: pin names not known; wires that end beside it: S9
  Hex_Digit_Display hex_digit_display_2 (.value(HEX4));  // open: dp
  Hex_Digit_Display hex_digit_display_3 (.value(HEX3));  // open: dp
  LED u_L6 (.in(L6));
  LED u_L5 (.in(L5));
  LED u_L7 (.in(L7));
  // DipSwitch #(.NSwitches(1)) S6: pin names not known; wires that end beside it: S6
  // DipSwitch #(.NSwitches(1)) S5: pin names not known; wires that end beside it: S5
  D_Flip_Flop d_ff_1 (.clk(clock_1_out), .D(S1), .Q(d_ff_1_q));  // open: Qn, preset, reset
  T_Flip_Flop t_ff_1 (.clk(clock_1_out), .T(S0), .Q(t_ff_1_q));  // open: Qn, preset, reset
  Hex_Digit_Display hex_digit_display_4 (.value(HEX1));  // open: dp
  Hex_Digit_Display hex_digit_display_5 (.value(HEX2));  // open: dp
  LED u_L4 (.in(L4));
  LED u_L2 (.in(L2));
  LED u_L3 (.in(L3));
  // DipSwitch #(.NSwitches(1)) S3: pin names not known; wires that end beside it: S3
  // DipSwitch #(.NSwitches(1)) S4: pin names not known; wires that end beside it: S4
  // DipSwitch #(.NSwitches(1)) S2: pin names not known; wires that end beside it: S2
  LED led_1 (.in(d_ff_1_q));
  LED led_2 (.in(t_ff_1_q));
  Hex_Digit_Display hex_digit_display_6 (.value(HEX0));  // open: dp
  LED u_L0 (.in(L0));
  LED u_L1 (.in(L1));
  // DipSwitch #(.NSwitches(1)) S0: pin names not known; wires that end beside it: S0
  // DipSwitch #(.NSwitches(1)) S1: pin names not known; wires that end beside it: S1
  Button u_K1 (.out(K1));
  Button u_K3 (.out(K3));
  Button u_K2 (.out(K2));
  Button u_K0 (.out(K0));
endmodule

module Ativ02 (
);

  wire clock_1_out, K0, K1, K2, K3, L0, L1, L2, L3, L4, L5, L6, L7, L8, L9, reg4_1_q1, reg4_1_q2, reg4_1_q3,
       reg4_1_q4, S0, S1, S2, S3, S4, S5, S6, S7, S8, S9;
  wire [3:0] HEX0, HEX1, HEX2, HEX3, HEX4, HEX5;

  // DipSwitch #(.NSwitches(1)) S9: pin names not known; wires that end beside it: S9
  Clock clock_1 (.out(clock_1_out));
  Hex_Digit_Display hex_digit_display_1 (.value(HEX5));  // open: dp
  Hex_Digit_Display hex_digit_display_2 (.value(HEX4));  // open: dp
  LED u_L9 (.in(L9));
  LED u_L8 (.in(L8));
  LED u_L7 (.in(L7));
  // DipSwitch #(.NSwitches(1)) S8: pin names not known; wires that end beside it: S8
  // DipSwitch #(.NSwitches(1)) S7: pin names not known; wires that end beside it: S7
  REG4 reg4_1 (
    .CLK(clock_1_out), .D1(S3), .D2(S2), .D3(S1), .D4(S0), .Q1(reg4_1_q1), .Q2(reg4_1_q2), .Q3(reg4_1_q3),
    .Q4(reg4_1_q4));  // open: PR, CLR, Q1_NOT, Q2_NOT, Q3_NOT, Q4_NOT
  Hex_Digit_Display hex_digit_display_3 (.value(HEX3));  // open: dp
  LED u_L6 (.in(L6));
  LED u_L5 (.in(L5));
  LED u_L4 (.in(L4));
  // DipSwitch #(.NSwitches(1)) S6: pin names not known; wires that end beside it: S6
  // DipSwitch #(.NSwitches(1)) S5: pin names not known; wires that end beside it: S5
  // DipSwitch #(.NSwitches(1)) S4: pin names not known; wires that end beside it: S4
  // Digital_Oscilloscope digital_oscilloscope_1: pin names not known; wires that end beside it: clock_1_out, reg4_1_q1, reg4_1_q2, reg4_1_q3, reg4_1_q4
  Hex_Digit_Display hex_digit_display_4 (.value(HEX1));  // open: dp
  Hex_Digit_Display hex_digit_display_5 (.value(HEX2));  // open: dp
  LED u_L2 (.in(L2));
  LED u_L3 (.in(L3));
  // DipSwitch #(.NSwitches(1)) S2: pin names not known; wires that end beside it: S2
  // DipSwitch #(.NSwitches(1)) S3: pin names not known; wires that end beside it: S3
  // DipSwitch #(.NSwitches(1)) S1: pin names not known; wires that end beside it: S1
  Hex_Digit_Display hex_digit_display_6 (.value(HEX0));  // open: dp
  LED u_L1 (.in(L1));
  LED u_L0 (.in(L0));
  // DipSwitch #(.NSwitches(1)) S0: pin names not known; wires that end beside it: S0
  Button u_K3 (.out(K3));
  Button u_K1 (.out(K1));
  Button u_K2 (.out(K2));
  Button u_K0 (.out(K0));
endmodule

module Ativ03 (
);

  wire K0, K1, K2, K3, L0, L1, L2, L3, L4, L5, L6, L7, L8, L9, S0, S1, S2, S3, S4, S5, S6, S7, S8, S9;
  wire [3:0] HEX0, HEX1, HEX2, HEX3, HEX4, HEX5;

  // DipSwitch #(.NSwitches(1)) S9: pin names not known; wires that end beside it: S9
  COUNTER8 counter8_1 (.CLK(S0), .Vcc(S1), .Q({HEX1, HEX0}));  // open: CLR
  Hex_Digit_Display hex_digit_display_1 (.value(HEX5));  // open: dp
  Hex_Digit_Display hex_digit_display_2 (.value(HEX4));  // open: dp
  LED u_L9 (.in(L9));
  LED u_L7 (.in(L7));
  LED u_L8 (.in(L8));
  // DipSwitch #(.NSwitches(1)) S8: pin names not known; wires that end beside it: S8
  // DipSwitch #(.NSwitches(1)) S7: pin names not known; wires that end beside it: S7
  Hex_Digit_Display hex_digit_display_3 (.value(HEX3));  // open: dp
  LED u_L6 (.in(L6));
  LED u_L4 (.in(L4));
  LED u_L5 (.in(L5));
  // DipSwitch #(.NSwitches(1)) S5: pin names not known; wires that end beside it: S5
  // DipSwitch #(.NSwitches(1)) S4: pin names not known; wires that end beside it: S4
  // DipSwitch #(.NSwitches(1)) S6: pin names not known; wires that end beside it: S6
  Hex_Digit_Display hex_digit_display_4 (.value(HEX2));  // open: dp
  Hex_Digit_Display hex_digit_display_5 (.value(HEX1));  // open: dp
  LED u_L3 (.in(L3));
  LED u_L2 (.in(L2));
  // DipSwitch #(.NSwitches(1)) S2: pin names not known; wires that end beside it: S2
  // DipSwitch #(.NSwitches(1)) S1: pin names not known; wires that end beside it: S1
  // DipSwitch #(.NSwitches(1)) S3: pin names not known; wires that end beside it: S3
  Hex_Digit_Display hex_digit_display_6 (.value(HEX0));  // open: dp
  LED u_L0 (.in(L0));
  LED u_L1 (.in(L1));
  // DipSwitch #(.NSwitches(1)) S0: pin names not known; wires that end beside it: S0
  Button u_K3 (.out(K3));
  Button u_K2 (.out(K2));
  Button u_K1 (.out(K1));
  Button u_K0 (.out(K0));

  // Notes on the sheet:
  //   Vcc
  //   CLK
endmodule

module Ativ04 (
);

  wire K0, K1, K2, K3, L0, L1, L2, L3, L4, L5, L6, L7, L8, L9, S0, S1, S2, S3, S4, S5, S6, S7, S8, S9;
  wire [3:0] HEX0, HEX1, HEX2, HEX3, HEX4, HEX5;
  wire [7:0] COUNTER_q;
  wire [15:0] ROM_data;

  // DipSwitch #(.NSwitches(1)) S9: pin names not known; wires that end beside it: S9
  Hex_Digit_Display hex_digit_display_1 (.value(HEX5));  // open: dp
  Hex_Digit_Display hex_digit_display_2 (.value(HEX4));  // open: dp
  LED u_L7 (.in(L7));
  LED u_L9 (.in(L9));
  LED u_L8 (.in(L8));
  // DipSwitch #(.NSwitches(1)) S8: pin names not known; wires that end beside it: S8
  // DipSwitch #(.NSwitches(1)) S7: pin names not known; wires that end beside it: S7
  COUNTER8 COUNTER (.CLK(S9), .Vcc(1'b1), .CLR(S0), .Q(COUNTER_q));
  Hex_Digit_Display hex_digit_display_3 (.value(HEX3));  // open: dp
  LED u_L4 (.in(L4));
  LED u_L6 (.in(L6));
  LED u_L5 (.in(L5));
  // DipSwitch #(.NSwitches(1)) S6: pin names not known; wires that end beside it: S6
  // DipSwitch #(.NSwitches(1)) S5: pin names not known; wires that end beside it: S5
  // DipSwitch #(.NSwitches(1)) S4: pin names not known; wires that end beside it: S4
  Hex_Digit_Display hex_digit_display_4 (.value(HEX1));  // open: dp
  Hex_Digit_Display hex_digit_display_5 (.value(HEX2));  // open: dp
  LED u_L3 (.in(L3));
  LED u_L2 (.in(L2));
  // DipSwitch #(.NSwitches(1)) S2: pin names not known; wires that end beside it: S2
  // DipSwitch #(.NSwitches(1)) S3: pin names not known; wires that end beside it: S3
  // DipSwitch #(.NSwitches(1)) S1: pin names not known; wires that end beside it: S1
  ROM #(.dataWidth(16), .Select("low")) ROM (.addr(COUNTER_q), .data(ROM_data));
  Hex_Digit_Display hex_digit_display_6 (.value(HEX0));  // open: dp
  LED u_L1 (.in(L1));
  LED u_L0 (.in(L0));
  // DipSwitch #(.NSwitches(1)) S0: pin names not known; wires that end beside it: S0
  Button u_K3 (.out(K3));
  REG16 REG16 (.D(ROM_data), .Clock(S9), .Q({HEX5, HEX4, HEX3, HEX2}));  // open: Preset, Clear
  Button u_K2 (.out(K2));
  Button u_K1 (.out(K1));
  Button u_K0 (.out(K0));

  // Notes on the sheet:
  //   CLK
  //   S0 = CLR, S9 = CLK
  //   contents of ROM (hex, n*v repeats v):
  //   6005 9101 6202 6304 c08 0 0 0 400 6001 9001 9002 6302 6102 9302 6200 6001 800
  //   CLR
endmodule

module Ativ06 (
);

  wire K0, K1, K2, K3, L0, L1, L2, L3, L4, L5, L6, L7, L8, L9, or_1_out, or_2_out, RESET_PC, RESET_REG, S0,
       S1, S2, S3, S4, S5, S6, S7, S8, S9;
  wire [1:0] CU_rgin, CU_rgto, CU_ula;
  wire [3:0] CU_x, HEX0, HEX1, HEX2, HEX3, HEX4, HEX5, multiplexer_1_out, Q_REG1, Q_REG2, TO_REG1, TO_REG2,
       ULA_r;
  wire [7:0] COUNTER_q;
  wire [15:0] REG16_q, ROM_data;

  Hex_Digit_Display hex_digit_display_1 (.value(HEX4));  // open: dp
  Hex_Digit_Display hex_digit_display_2 (.value(HEX5));  // open: dp
  LED u_L8 (.in(L8));
  LED u_L7 (.in(L7));
  LED u_L9 (.in(L9));
  // DipSwitch #(.NSwitches(1)) S9: pin names not known; wires that end beside it: S9
  // DipSwitch #(.NSwitches(1)) S7: pin names not known; wires that end beside it: S7
  // DipSwitch #(.NSwitches(1)) S8: pin names not known; wires that end beside it: S8
  Hex_Digit_Display hex_digit_display_3 (.value(HEX3));  // open: dp
  LED u_L5 (.in(L5));
  LED u_L6 (.in(L6));
  // DipSwitch #(.NSwitches(1)) S6: pin names not known; wires that end beside it: S6
  // DipSwitch #(.NSwitches(1)) S5: pin names not known; wires that end beside it: S5
  // DipSwitch #(.NSwitches(1)) S4: pin names not known; wires that end beside it: S4
  or or_1 (or_1_out, S0, RESET_PC);
  Hex_Digit_Display hex_digit_display_4 (.value(HEX2));  // open: dp
  Hex_Digit_Display hex_digit_display_5 (.value(HEX1));  // open: dp
  LED u_L4 (.in(L4));
  LED u_L2 (.in(L2));
  LED u_L3 (.in(L3));
  // DipSwitch #(.NSwitches(1)) S2: pin names not known; wires that end beside it: S2
  // DipSwitch #(.NSwitches(1)) S3: pin names not known; wires that end beside it: S3
  COUNTER8 COUNTER (.CLK(S9), .Vcc(1'b1), .CLR(or_1_out), .Q(COUNTER_q));
  Hex_Digit_Display hex_digit_display_6 (.value(HEX0));  // open: dp
  LED u_L0 (.in(L0));
  LED u_L1 (.in(L1));
  // DipSwitch #(.NSwitches(1)) S1: pin names not known; wires that end beside it: S1
  // DipSwitch #(.NSwitches(1)) S0: pin names not known; wires that end beside it: S0
  Button u_K1 (.out(K1));
  Button u_K3 (.out(K3));
  Button u_K2 (.out(K2));
  ROM #(.dataWidth(16), .Select("low")) ROM (.addr(COUNTER_q), .data(ROM_data));
  REG16 REG16 (.D(ROM_data), .Clock(S9), .Q(REG16_q));  // open: Preset, Clear
  REG4_Grouped REG1 (.CLK(S9), .D(TO_REG1), .Clear(or_2_out), .Q(Q_REG1));  // open: Preset, Q_NOT
  Button u_K0 (.out(K0));
  Multiplexer #(.select(2), .width(4), .enable("false")) multiplexer_1 (
    .in0(4'b0000), .in1(Q_REG1), .in2(Q_REG2), .in3(4'b0000), .out(multiplexer_1_out), .sel(CU_rgin));
  CONTROL_UNIT CU (
    .dataBus_16(REG16_q), .RgIN(CU_rgin), .X(CU_x), .ULA(CU_ula), .RgTO(CU_rgto), .JMP_RESET_REG(RESET_REG),
    .JMP_RESET_PC(RESET_PC));  // open: NULL, JMP_ULA, JMP_X
  or or_2 (or_2_out, S0, RESET_PC);
  ULA ULA (.A(multiplexer_1_out), .B(CU_x), .Op(CU_ula), .R(ULA_r));
  REG4_Grouped REG2 (.CLK(S9), .D(TO_REG2), .Clear(or_2_out), .Q(Q_REG2));  // open: Preset, Q_NOT
  // Digital_Oscilloscope digital_oscilloscope_1: pin names not known; wires that end beside it: S9, ULA_r[0], ULA_r[1], ULA_r[2], ULA_r[3]
  Demultiplexer #(.select(2), .width(4), .enable("false")) demultiplexer_1 (
    .out1(TO_REG1), .out2(TO_REG2), .in(ULA_r), .sel(CU_rgto));  // open: out0, out3
  // Digital_Oscilloscope digital_oscilloscope_2: pin names not known; wires that end beside it: S9, Q_REG2[0], Q_REG2[1], Q_REG2[2]
  // Digital_Oscilloscope digital_oscilloscope_3: pin names not known; wires that end beside it: Q_REG2[3], S9, TO_REG2[0], TO_REG2[1], TO_REG2[2]
  // Digital_Oscilloscope digital_oscilloscope_4: pin names not known; wires that end beside it: TO_REG2[3], S9, Q_REG1[0], Q_REG1[1], Q_REG1[2]
  // Digital_Oscilloscope digital_oscilloscope_5: pin names not known; wires that end beside it: Q_REG1[3], S9, TO_REG1[0], TO_REG1[1], TO_REG1[2], TO_REG1[3]

  // Notes on the sheet:
  //   S0 = CLR, S9 = CLK
  //   CLK
  //   Counter sem JUMP
  //   CLR
  //   contents of ROM (hex, n*v repeats v):
  //   4103 9202 6001 4307 0 800 238*0 1111
  //   Escolhe o Reg que vai para ULA
  //   A = Q_RgIN
  //   B = X
  //   Escolhe o Reg no qual será guardado o resultado
  //   ULA OUT
  //   REG2 IN
  //   REG2 OUT
  //   REG1 OUT
  //   REG1 IN
endmodule

module COUNTER8_JMP_UNIT (
  input  X,
  input  CLK,
  input  T,
  input  CLR,
  input  JMP,
  output Q,
  output Q_NOT
);

  wire and_1_out, and_2_out, not_1_out, or_1_out;

  and and_1 (and_1_out, X, JMP);
  T_Flip_Flop t_ff_1 (.clk(CLK), .T(T), .Q(Q), .Qn(Q_NOT), .preset(and_1_out), .reset(or_1_out));
  or or_1 (or_1_out, CLR, and_2_out);
  and and_2 (and_2_out, not_1_out, JMP);
  not not_1 (not_1_out, X);
endmodule

module AtivRelatorio (
);

  wire K0, K1, K2, K3, L0, L1, L2, L3, L4, L5, L6, L7, L8, L9, or_1_out, or_2_out, RESET_PC, RESET_REG, S0,
       S1, S2, S3, S4, S5, S6, S7, S8, S9;
  wire [1:0] CU_rgin, CU_rgto, CU_ula;
  wire [3:0] CU_x, HEX0, HEX1, HEX2, HEX3, HEX4, HEX5, multiplexer_1_out, Q_REG1, Q_REG2, TO_REG1, TO_REG2,
       ULA_r;
  wire [15:0] ROM_data;

  Hex_Digit_Display hex_digit_display_1 (.value(HEX5));  // open: dp
  LED u_L9 (.in(L9));
  LED u_L8 (.in(L8));
  // DipSwitch #(.NSwitches(1)) S8: pin names not known; wires that end beside it: S8
  // DipSwitch #(.NSwitches(1)) S9: pin names not known; wires that end beside it: S9
  Hex_Digit_Display hex_digit_display_2 (.value(HEX4));  // open: dp
  Hex_Digit_Display hex_digit_display_3 (.value(HEX3));  // open: dp
  LED u_L7 (.in(L7));
  LED u_L6 (.in(L6));
  LED u_L5 (.in(L5));
  // DipSwitch #(.NSwitches(1)) S7: pin names not known; wires that end beside it: S7
  // DipSwitch #(.NSwitches(1)) S5: pin names not known; wires that end beside it: S5
  // DipSwitch #(.NSwitches(1)) S6: pin names not known; wires that end beside it: S6
  or or_1 (or_1_out, S0, RESET_PC);
  Hex_Digit_Display hex_digit_display_4 (.value(HEX2));  // open: dp
  LED u_L3 (.in(L3));
  LED u_L4 (.in(L4));
  // DipSwitch #(.NSwitches(1)) S2: pin names not known; wires that end beside it: S2
  // DipSwitch #(.NSwitches(1)) S3: pin names not known; wires that end beside it: S3
  // DipSwitch #(.NSwitches(1)) S4: pin names not known; wires that end beside it: S4
  COUNTER8 COUNTER (.CLK(S9), .Vcc(1'b1), .CLR(or_1_out), .Q({L7, L6, L5, L4, L3, L2, L1, L0}));
  Hex_Digit_Display hex_digit_display_5 (.value(HEX1));  // open: dp
  Hex_Digit_Display hex_digit_display_6 (.value(HEX0));  // open: dp
  LED u_L0 (.in(L0));
  LED u_L2 (.in(L2));
  LED u_L1 (.in(L1));
  // DipSwitch #(.NSwitches(1)) S1: pin names not known; wires that end beside it: S1
  // DipSwitch #(.NSwitches(1)) S0: pin names not known; wires that end beside it: S0
  Button u_K2 (.out(K2));
  Button u_K3 (.out(K3));
  REG16 REG16 (.D(ROM_data), .Clock(S9), .Q({HEX5, HEX4, HEX3, HEX2}));  // open: Preset, Clear
  ROM #(.dataWidth(16), .Select("low")) ROM (.addr({L7, L6, L5, L4, L3, L2, L1, L0}), .data(ROM_data));
  REG4_Grouped REG1 (.CLK(S9), .D(TO_REG1), .Clear(or_2_out), .Q(Q_REG1));  // open: Preset, Q_NOT
  Button u_K0 (.out(K0));
  Button u_K1 (.out(K1));
  Multiplexer #(.select(2), .width(4), .enable("false")) multiplexer_1 (
    .in0(4'b0000), .in1(Q_REG1), .in2(Q_REG2), .in3(4'b0000), .out(multiplexer_1_out), .sel(CU_rgin));
  CONTROL_UNIT CU (
    .dataBus_16({HEX5, HEX4, HEX3, HEX2}), .RgIN(CU_rgin), .X(CU_x), .ULA(CU_ula), .RgTO(CU_rgto),
    .JMP_RESET_REG(RESET_REG), .JMP_RESET_PC(RESET_PC));  // open: NULL, JMP_ULA, JMP_X
  or or_2 (or_2_out, S0, RESET_PC);
  ULA ULA (.A(multiplexer_1_out), .B(CU_x), .Op(CU_ula), .R(ULA_r));
  REG4_Grouped REG2 (.CLK(S9), .D(TO_REG2), .Clear(or_2_out), .Q(Q_REG2));  // open: Preset, Q_NOT
  Demultiplexer #(.select(2), .width(4), .enable("false")) demultiplexer_1 (
    .out1(TO_REG1), .out2(TO_REG2), .in(ULA_r), .sel(CU_rgto));  // open: out0, out3
  // Digital_Oscilloscope digital_oscilloscope_1: pin names not known; wires that end beside it: S9, L0, L1, L2, L3, L4
  // Digital_Oscilloscope digital_oscilloscope_2: pin names not known; wires that end beside it: L5, L6, L7, S9, HEX2[0], HEX2[1], HEX2[2], HEX2[3], HEX3[0], HEX3[1], HEX3[2], HEX3[3], HEX4[0], HEX4[1]

  // Notes on the sheet:
  //   S0 = CLR, S9 = CLK
  //   CLK
  //   Counter sem JUMP
  //   CLR
  //   contents of ROM (hex, n*v repeats v):
  //   6005 9101 6202 6304 c08 0 0 0 400 6001 9001 9002 6302 6102 9302 6200 6001 800
  //   Escolhe o Reg que vai para ULA
  //   A = Q_RgIN
  //   B = X
  //   Escolhe o Reg no qual será guardado o resultado
  //   CONTADOR
  //   MEMÓRIA
endmodule
